// Logisim project LED计数电路.circ as structural Verilog: 4 circuits, main circuit LED计数电路
module \LED计数电路  (
  input  in_1,
  input  in_2,
  input  in_3,
  input  in_4,
  input  in_5,
  output out_6,
  output out_7,
  output out_8,
  output out_9,
  output out_10
);

  or or_1 (out_6, in_1, in_2, in_3, in_4, in_5);
  or or_2 (out_7, in_2, in_3, in_4, in_5);
  or or_3 (out_8, in_3, in_4, in_5);
  or or_4 (out_9, in_4, in_5);

  assign out_10 = in_5;

  // Notes on the sheet:
  //   LED计数电路
endmodule

module \LED计数测试  (
  output out_1,
  output out_2,
  output out_3,
  output out_4,
  output out_5
);

  wire button_1_out, button_2_out, button_3_out, button_4_out, button_5_out;
  wire [2:0] \n5输入按键编码器_1_out1 ;

  Button button_1 (.out(button_1_out));
  Button button_2 (.out(button_2_out));
  Button button_3 (.out(button_3_out));
  Button button_4 (.out(button_4_out));
  Button button_5 (.out(button_5_out));
  \LED计数电路  \led计数电路_1  (
    .in_1(button_1_out), .in_2(button_2_out), .in_3(button_3_out), .in_4(button_4_out), .in_5(button_5_out),
    .out_6(out_1), .out_7(out_2), .out_8(out_3), .out_9(out_4), .out_10(out_5));
  \_5输入按键编码器  \u_5输入按键编码器_1  (
    .In1(button_1_out), .In2(button_2_out), .In3(button_3_out), .In4(button_4_out), .In5(button_5_out),
    .Out1(\n5输入按键编码器_1_out1 [0]), .Out2(\n5输入按键编码器_1_out1 [1]), .Out3(\n5输入按键编码器_1_out1 [2]));
  // Probe on \n5输入按键编码器_1_out1 
  Hex_Digit_Display hex_digit_display_1 (.value({1'b0, \n5输入按键编码器_1_out1 }), .dp(1'b1));

  // Notes on the sheet:
  //   LED计数测试
  //   5输入按键编码器
endmodule

module \七段数码管显示驱动  (
  input  x0,
  input  x1,
  input  x2,
  input  x3,
  output Seg_1,
  output Seg_2,
  output Seg_3,
  output Seg_4,
  output Seg_5,
  output Seg_6,
  output Seg_7
);

  wire and_1_out, and_2_out, and_3_out, and_4_out, and_5_out, and_6_out, and_7_out, and_8_out, and_9_out,
       and_10_out, and_11_out, and_12_out, and_13_out, and_14_out, and_15_out, and_16_out, and_17_out,
       and_18_out, and_19_out, and_20_out, and_21_out, and_22_out, and_23_out, and_24_out, and_25_out,
       and_26_out, not_1_out, not_2_out, not_3_out, not_4_out, not_5_out, not_6_out, not_7_out, not_8_out,
       not_9_out, not_10_out, not_11_out, not_12_out, not_13_out, not_14_out, not_15_out, not_16_out,
       not_17_out, not_18_out, not_19_out, not_20_out, not_21_out, not_22_out, not_23_out, not_24_out,
       not_25_out, not_26_out, not_27_out, not_28_out, not_29_out, not_30_out, not_31_out, not_32_out,
       not_33_out, not_34_out, not_35_out, not_36_out, not_37_out, not_38_out, not_39_out, not_40_out,
       not_41_out, not_42_out, not_43_out, not_44_out, not_45_out, not_46_out, not_47_out, not_48_out,
       not_49_out, not_50_out, not_51_out, not_52_out;

  not not_1 (not_1_out, x0);
  not not_2 (not_2_out, x1);
  and and_1 (and_1_out, not_1_out, not_2_out, x2);
  not not_3 (not_3_out, x0);
  and and_2 (and_2_out, not_3_out, x1, not_4_out);
  not not_4 (not_4_out, x2);
  not not_5 (not_5_out, x0);
  and and_3 (and_3_out, not_5_out, x1, not_6_out);
  not not_6 (not_6_out, x3);
  not not_7 (not_7_out, x1);
  and and_4 (and_4_out, x0, not_7_out, not_8_out);
  not not_8 (not_8_out, x2);
  not not_9 (not_9_out, x0);
  not not_10 (not_10_out, x2);
  and and_5 (and_5_out, not_9_out, not_10_out, not_11_out);
  not not_11 (not_11_out, x3);
  not not_12 (not_12_out, x0);
  and and_6 (and_6_out, not_12_out, x1, not_13_out);
  not not_13 (not_13_out, x2);
  not not_14 (not_14_out, x0);
  and and_7 (and_7_out, not_14_out, x1, not_15_out);
  not not_15 (not_15_out, x3);
  not not_16 (not_16_out, x1);
  and and_8 (and_8_out, x0, not_16_out, not_17_out);
  not not_17 (not_17_out, x2);
  not not_18 (not_18_out, x0);
  and and_9 (and_9_out, not_18_out, not_19_out, not_20_out);
  not not_19 (not_19_out, x1);
  not not_20 (not_20_out, x3);
  not not_21 (not_21_out, x0);
  and and_10 (and_10_out, not_21_out, x2);
  not not_22 (not_22_out, x0);
  and and_11 (and_11_out, not_22_out, x1, x3);
  not not_23 (not_23_out, x1);
  and and_12 (and_12_out, x0, not_23_out, not_24_out);
  not not_24 (not_24_out, x2);
  not not_25 (not_25_out, x0);
  and and_13 (and_13_out, not_25_out, not_26_out);
  not not_26 (not_26_out, x1);
  not not_27 (not_27_out, x0);
  not not_28 (not_28_out, x2);
  and and_14 (and_14_out, not_27_out, not_28_out, not_29_out);
  not not_29 (not_29_out, x3);
  not not_30 (not_30_out, x1);
  and and_15 (and_15_out, not_30_out, not_31_out);
  not not_31 (not_31_out, x2);
  not not_32 (not_32_out, x0);
  and and_16 (and_16_out, not_32_out, x2, x3);
  not not_33 (not_33_out, x1);
  and and_17 (and_17_out, not_33_out, not_34_out, not_35_out);
  not not_34 (not_34_out, x2);
  not not_35 (not_35_out, x3);
  not not_36 (not_36_out, x0);
  and and_18 (and_18_out, not_36_out, x2, not_37_out);
  not not_37 (not_37_out, x3);
  not not_38 (not_38_out, x0);
  not not_39 (not_39_out, x1);
  not not_40 (not_40_out, x3);
  not not_41 (not_41_out, x0);
  not not_42 (not_42_out, x1);
  not not_43 (not_43_out, x0);
  not not_44 (not_44_out, x3);
  not not_45 (not_45_out, x0);
  not not_46 (not_46_out, x2);
  not not_47 (not_47_out, x1);
  not not_48 (not_48_out, x2);
  not not_49 (not_49_out, x1);
  and and_19 (and_19_out, not_49_out, not_50_out);
  not not_50 (not_50_out, x2);
  not not_51 (not_51_out, x0);
  and and_20 (and_20_out, not_51_out, x3);
  not not_52 (not_52_out, x0);
  and and_21 (and_21_out, not_52_out, x1);
  or or_1 (Seg_1, and_1_out, and_2_out, and_3_out, and_4_out);
  or or_2 (Seg_2, and_5_out, and_6_out, and_7_out, and_8_out);
  or or_3 (Seg_3, and_9_out, and_10_out, and_11_out, and_12_out);
  or or_4 (Seg_4, and_13_out, and_14_out, and_15_out, and_16_out);
  or or_5 (Seg_5, and_17_out, and_18_out);
  and and_22 (and_22_out, not_38_out, not_39_out, not_40_out);
  and and_23 (and_23_out, not_41_out, not_42_out, x2);
  and and_24 (and_24_out, not_43_out, x2, not_44_out);
  and and_25 (and_25_out, not_45_out, x1, not_46_out, x3);
  and and_26 (and_26_out, x0, not_47_out, not_48_out);
  or or_6 (Seg_7, and_19_out, and_20_out, and_21_out);
  or or_7 (Seg_6, and_22_out, and_23_out, and_24_out, and_25_out, and_26_out);
endmodule

module \_5输入按键编码器  (
  input  In1,
  input  In2,
  input  In3,
  input  In4,
  input  In5,
  output Out1,
  output Out2,
  output Out3
);

  wire and_1_out, and_2_out, and_3_out, and_4_out, and_5_out, and_6_out, and_7_out, and_8_out, and_9_out,
       and_10_out, and_11_out, and_12_out, not_1_out, not_2_out, not_3_out, not_4_out, not_5_out, not_6_out,
       not_7_out, not_8_out, not_9_out, not_10_out, not_11_out, not_12_out;

  not not_1 (not_1_out, In4);
  not not_2 (not_2_out, In4);
  not not_3 (not_3_out, In2);
  not not_4 (not_4_out, In4);
  not not_5 (not_5_out, In1);
  not not_6 (not_6_out, In2);
  not not_7 (not_7_out, In5);
  not not_8 (not_8_out, In4);
  not not_9 (not_9_out, In5);
  not not_10 (not_10_out, In4);
  not not_11 (not_11_out, In5);
  not not_12 (not_12_out, In3);
  and and_1 (and_1_out, not_1_out, In5);
  and and_2 (and_2_out, In3, not_2_out);
  and and_3 (and_3_out, In3, In5);
  and and_4 (and_4_out, In2, In5);
  and and_5 (and_5_out, In1, not_3_out, not_4_out);
  and and_6 (and_6_out, In1, In5);
  and and_7 (and_7_out, not_5_out, not_6_out, In3, not_7_out);
  and and_8 (and_8_out, In3, not_8_out, not_9_out);
  and and_9 (and_9_out, In2, not_10_out, not_11_out);
  and and_10 (and_10_out, not_12_out, In4);
  and and_11 (and_11_out, In2, In4);
  and and_12 (and_12_out, In1, In4);
  or or_1 (Out1, and_1_out, and_2_out, and_3_out, and_4_out, and_5_out, and_6_out);
  or or_2 (Out2, and_7_out, and_8_out, and_9_out);
  or or_3 (Out3, In5, and_10_out, and_11_out, and_12_out);
endmodule
